# Fritzing sketch Bot Connections (saved by Fritzing 0.9.3b)
breadboards: 1

parts:
  Part1 = Arduino Uno (Rev3)
  S1 = H-Bridge with L298N
  GY3 = MPU-6050 Board GY-521 [form="♀ (female)" package=THT]
  M1 = DC Motor
  M2 = DC Motor
  Part2 = Bluetooth HC-05 Macho
  VCC1 = Battery block 9V

nets:
  N1: Part1.A4/SDA, GY3.pin4
  N2: Part1.A5/SCL, GY3.pin3
  N3: Part1.D8, S1.IN2
  N4: Part1.D9_PWM, S1.IN1
  N5: Part1.D10_PWM/SS, S1.ENA
  N6: Part1.D0/RX, Part2.TXD
  N7: Part1.D1/TX, Part2.RXD
  N8: Part1.D2, GY3.pin8
  N9: Part1.D5_PWM, S1.ENB
  N10: Part1.D6_PWM, S1.IN4
  N11: Part1.D7, S1.IN3
  5V: Part1.5V, Part2.VCC
  GND: Part1.GND, S1.GND, Part2.GND, VCC1.-
  N12: S1.12V, VCC1.+
  N13: S1.M1-01, M2.pin_2
  N14: S1.M1-02, M2.pin_1
  N15: S1.M2-01, M1.pin_2
  N16: S1.M2-02, M1.pin_1

custom parts:
  H-Bridge with L298N: h-bridge
  MPU-6050 Board GY-521: Acelerometro y Giroscopio MPU-6050 Board GY-521
