# Fritzing sketch Calibration (saved by Fritzing 0.9.3b)
breadboards: 1

parts:
  GY3 = MPU-6050 Board GY-521 [form="♀ (female)" package=THT]
  Part1 = Arduino Uno (Rev3)

nets:
  N1: GY3.pin1, Part1.3V3
  N2: GY3.pin2, Part1.GND
  N3: GY3.pin3, Part1.A5/SCL
  N4: GY3.pin4, Part1.A4/SDA
  N5: GY3.pin8, Part1.D2

custom parts:
  MPU-6050 Board GY-521: Acelerometro y Giroscopio MPU-6050 Board GY-521
