# Fritzing sketch L298N Test (saved by Fritzing 0.9.3b)

parts:
  Part1 = Arduino Uno (Rev3)
  S1 = H-Bridge with L298N
  VCC1 = Battery block 9V
  M1 = DC Motor

nets:
  N1: Part1.D8, S1.IN1
  N2: Part1.D11_PWM/MOSI, S1.ENA
  N3: Part1.D7, S1.IN2
  GND: Part1.GND, S1.GND, VCC1.-
  VIN: Part1.VIN, S1.5V
  N4: S1.12V, VCC1.+
  N5: S1.M1-01, M1.pin_2
  N6: S1.M1-02, M1.pin_1

custom parts:
  H-Bridge with L298N: h-bridge
